# Fritzing sketch diagram with pcb - Copy (saved by Fritzing 0.9.3b)
circuit board: 8.29cm x 6.61351cm

parts:
  NODEmcu = ESP8266 NodeMCU LoLin module
  Buzzer = Piezo Speaker
  Power_Jack = Power Jack [package=power_jack_slot]
  A1 = PMS5003

nets:
  N1: NODEmcu.D0, Buzzer.pin2
  N2: NODEmcu.D3, A1.Pin_4
  N3: NODEmcu.D4, A1.Pin_5
  N4: NODEmcu.3V3, A1.Pin_1
  GND: NODEmcu.GND, Buzzer.pin1, Power_Jack.GNDBREAK, Power_Jack.GND, A1.Pin_2
  N5: NODEmcu.Vin, Power_Jack.PWR

notes:
  PMS 5003
  BUZZER
  Power Supply

custom parts:
  ESP8266 NodeMCU LoLin module: ESP8266 based NodeMCU
  PMS5003: PMS5003 is a kind of digital and universal particle concentration sensor, which can be used to obtain the number of suspended particles in the air.
