# Fritzing sketch diagram with pcb (saved by Fritzing 0.9.3b)
circuit board: 8.84317cm x 6.87216cm

parts:
  NODEmcu = ESP8266 NodeMCU LoLin module
  Buzzer = Piezo Speaker
  Power_Jack = Power Jack [package=power_jack_slot]
  VCC_GND_SET_RXD_TXD_RST_NC_NC = Generic female header - 8 pins [form="♀ (female)" package=THT]
  TX_RX_VCC_GND = Generic female header - 4 pins [form="♀ (female)" package=THT]

nets:
  N1: NODEmcu.D0, Buzzer.pin2
  N2: NODEmcu.D2, VCC_GND_SET_RXD_TXD_RST_NC_NC.TXD, TX_RX_VCC_GND.TX
  N3: NODEmcu.D3, VCC_GND_SET_RXD_TXD_RST_NC_NC.RXD, TX_RX_VCC_GND.RX
  VCC: NODEmcu.3V3, VCC_GND_SET_RXD_TXD_RST_NC_NC.VCC, TX_RX_VCC_GND.VCC
  GND: NODEmcu.GND, Buzzer.pin1, Power_Jack.GNDBREAK, Power_Jack.GND, VCC_GND_SET_RXD_TXD_RST_NC_NC.GND, TX_RX_VCC_GND.GND
  N4: NODEmcu.Vin, Power_Jack.PWR

custom parts:
  ESP8266 NodeMCU LoLin module: ESP8266 based NodeMCU
  Generic female header - 8 pins: Generic female header
  Generic female header - 4 pins: Generic female header
