# Fritzing sketch Diagram (saved by Fritzing 0.9.3b)
breadboards: 2

parts:
  U1 = ESP8266 NodeMCU LoLin module
  Part1 = BH1750
  M1 = BME680 Module [part_number=CJMCU-680]
  J1 = Piezo Speaker

nets:
  N1: U1.D0, J1.pin2
  N2: U1.D1, Part1.SCL, M1.SCL
  N3: U1.D2, Part1.SDA, M1.SDA
  VCC: U1.3V3, Part1.VCC, M1.VCC, M1.CS
  GND: U1.GND, Part1.GND, M1.GND, J1.pin1

custom parts:
  ESP8266 NodeMCU LoLin module: ESP8266 based NodeMCU
  BH1750: Light Sensor
  BME680 Module: Bosch BME680 Development Module The BME680 is a digital 4-in-1 sensor that measures air quality [gas], humidity, pressure and temperature. Links: BME680 product datasheet
