# Fritzing sketch diagram v2 (saved by Fritzing 0.9.3b)
circuit board: 9.81721cm x 10.173cm

parts:
  BME680 = BME680 Module [part_number=CJMCU-680]
  ESP8266 = ESP8266 NodeMCU LoLin module
  BH1750 = BH1750
  Power_Jack = Power Jack [package=power_jack_slot]
  Buzzer = Piezo Speaker

nets:
  VCC: BME680.VCC, BME680.CS, ESP8266.3V3, BH1750.VCC
  GND: BME680.GND, ESP8266.GND, BH1750.GND, Power_Jack.GNDBREAK, Power_Jack.GND, Buzzer.pin1
  N1: BME680.SCL, ESP8266.D1, BH1750.SCL
  N2: BME680.SDA, ESP8266.D2, BH1750.SDA
  N3: ESP8266.D0, Buzzer.pin2
  N4: ESP8266.Vin, Power_Jack.PWR

notes:
  BH1750
  BME680
  BUZZER
  Power Supply

custom parts:
  BME680 Module: Bosch BME680 Development Module The BME680 is a digital 4-in-1 sensor that measures air quality [gas], humidity, pressure and temperature. Links: BME680 product datasheet
  ESP8266 NodeMCU LoLin module: ESP8266 based NodeMCU
  BH1750: Light Sensor
